// Logisim project oblArqui.circ as structural Verilog: 15 circuits, main circuit main
module main (
);

  wire button_1_out, button_2_out, button_3_out, button_4_out, button_5_out, button_6_out, button_7_out,
       contadorbin_1_led1, contadorbin_1_led2, contadorbin_1_led3, contadorbin_1_led4, contadorbin_1_led5,
       contadorbin_1_led6, contadorbin_1_led7, contadorbin_1_led8, contadorbin_1_led9, contadorbin_1_led10,
       guardarnuevoestado_1_colisionder, guardarnuevoestado_1_colisionizq, guardarnuevoestado_1_colisiony,
       guardarnuevoestado_1_next_bit_trigger, manejovelocidades_1_salida, puntajerecord_1_led1,
       puntajerecord_1_led2, puntajerecord_1_led3, puntajerecord_1_led4, puntajerecord_1_led5,
       puntajerecord_1_led6, puntajerecord_1_led7, puntajerecord_1_led8, puntajerecord_1_led9,
       puntajerecord_1_led10, R_out, Reloj;
  wire [2:0] movimientocuadrado_1_colactual;
  wire [3:0] contador2_1_puntos1, contador2_1_puntos2, contador2_1_puntos3, contador2_1_puntos4,
       puntajerecordhexa_1_record1, puntajerecordhexa_1_record2, puntajerecordhexa_1_record3,
       puntajerecordhexa_1_record4;
  wire [4:0] movimientocuadrado_1_inicio;
  wire [7:0] guardarnuevoestado_1_col_0, guardarnuevoestado_1_col_1, guardarnuevoestado_1_col_2,
       guardarnuevoestado_1_col_3, guardarnuevoestado_1_col_4, mergetableros_1_c0, mergetableros_1_c1,
       mergetableros_1_c2, mergetableros_1_c3, mergetableros_1_c4, movimientocuadrado_1_col0,
       movimientocuadrado_1_col1, movimientocuadrado_1_col2, movimientocuadrado_1_col3,
       movimientocuadrado_1_col4, movimientocuadrado_1_filaactual;

  Clock clock_1 (.out(Reloj));
  ManejoVelocidades manejovelocidades_1 (
    .clk(Reloj), .entrada(button_4_out), .reset(button_6_out), .salida(manejovelocidades_1_salida));
  movimientoCuadrado movimientocuadrado_1 (
    .colisionY(guardarnuevoestado_1_colisiony), .strart(button_1_out), .Clock(manejovelocidades_1_salida),
    .izq(button_2_out), .der(button_3_out), .colisionIzq(guardarnuevoestado_1_colisionizq),
    .colisionDer(guardarnuevoestado_1_colisionder), .inicio(movimientocuadrado_1_inicio),
    .col0(movimientocuadrado_1_col0), .col1(movimientocuadrado_1_col1), .col2(movimientocuadrado_1_col2),
    .col3(movimientocuadrado_1_col3), .col4(movimientocuadrado_1_col4),
    .filaActual(movimientocuadrado_1_filaactual), .colActual(movimientocuadrado_1_colactual));
  Button button_1 (.out(button_1_out));
  DotMatrix #(.matrixrows(1)) dotmatrix_1 (
    .col0(movimientocuadrado_1_inicio[4]), .col1(movimientocuadrado_1_inicio[3]),
    .col2(movimientocuadrado_1_inicio[2]), .col3(movimientocuadrado_1_inicio[1]),
    .col4(movimientocuadrado_1_inicio[0]));
  Button button_2 (.out(button_2_out));
  DotMatrix #(.matrixrows(8)) dotmatrix_2 (
    .col0(mergetableros_1_c0), .col1(mergetableros_1_c1), .col2(mergetableros_1_c2),
    .col3(mergetableros_1_c3), .col4(mergetableros_1_c4));
  Button button_3 (.out(button_3_out));
  Button R (.out(R_out));
  mergeTableros mergetableros_1 (
    .MC_C0(movimientocuadrado_1_col0), .MC_C1(movimientocuadrado_1_col1), .MC_C2(movimientocuadrado_1_col2),
    .MC_C3(movimientocuadrado_1_col3), .MC_C4(movimientocuadrado_1_col4),
    .GNE_C0(guardarnuevoestado_1_col_0), .GNE_C1(guardarnuevoestado_1_col_1),
    .GNE_C2(guardarnuevoestado_1_col_2), .GNE_C3(guardarnuevoestado_1_col_3),
    .GNE_C4(guardarnuevoestado_1_col_4), .C0(mergetableros_1_c0), .C1(mergetableros_1_c1),
    .C2(mergetableros_1_c2), .C3(mergetableros_1_c3), .C4(mergetableros_1_c4));
  guardarNuevoEstado guardarnuevoestado_1 (
    .CLK(Reloj), .RESET(R_out), .WRITE_ENABLE(manejovelocidades_1_salida),
    .Y_POS(movimientocuadrado_1_filaactual), .X_POS(movimientocuadrado_1_colactual),
    .COL_0(guardarnuevoestado_1_col_0), .COL_1(guardarnuevoestado_1_col_1),
    .COL_2(guardarnuevoestado_1_col_2), .COL_3(guardarnuevoestado_1_col_3),
    .COL_4(guardarnuevoestado_1_col_4), .NEXT_BIT_TRIGGER(guardarnuevoestado_1_next_bit_trigger),
    .colisionY(guardarnuevoestado_1_colisiony), .colisionDer(guardarnuevoestado_1_colisionder),
    .colisionIzq(guardarnuevoestado_1_colisionizq));
  DetectorFilaCompleta detectorfilacompleta_1 ();  // open: COL0, COL1, COL2, COL3, COL4
  Button button_4 (.out(button_4_out));
  Button button_5 (.out(button_5_out));
  Button button_6 (.out(button_6_out));
  LED led_1 (.in(contadorbin_1_led1));
  contadorBin contadorbin_1 (
    .Entrada(button_4_out), .Suma5(button_5_out), .Reset(button_6_out), .Clock(Reloj),
    .Led1(contadorbin_1_led1), .Led2(contadorbin_1_led2), .Led3(contadorbin_1_led3),
    .Led4(contadorbin_1_led4), .Led5(contadorbin_1_led5), .Led6(contadorbin_1_led6),
    .Led7(contadorbin_1_led7), .Led8(contadorbin_1_led8), .Led9(contadorbin_1_led9),
    .Led10(contadorbin_1_led10));
  LED led_2 (.in(contadorbin_1_led2));
  LED led_3 (.in(contadorbin_1_led3));
  LED led_4 (.in(contadorbin_1_led4));
  LED led_5 (.in(contadorbin_1_led5));
  LED led_6 (.in(contadorbin_1_led6));
  LED led_7 (.in(contadorbin_1_led7));
  LED led_8 (.in(contadorbin_1_led8));
  LED led_9 (.in(contadorbin_1_led9));
  LED led_10 (.in(contadorbin_1_led10));
  Button button_7 (.out(button_7_out));
  Hex_Digit_Display hex_digit_display_1 (.value(contador2_1_puntos4));  // open: dp
  contador2 contador2_1 (
    .Reset(button_6_out), .Suma5(button_5_out), .Sumar1(button_4_out), .Clock(Reloj),
    .Puntos4(contador2_1_puntos4), .Puntos3(contador2_1_puntos3), .Puntos2(contador2_1_puntos2),
    .Puntos1(contador2_1_puntos1));
  Hex_Digit_Display hex_digit_display_2 (.value(contador2_1_puntos3));  // open: dp
  Hex_Digit_Display hex_digit_display_3 (.value(contador2_1_puntos2));  // open: dp
  Hex_Digit_Display hex_digit_display_4 (.value(contador2_1_puntos1));  // open: dp
  LED led_11 (.in(puntajerecord_1_led1));
  PuntajeRecord puntajerecord_1 (
    .LedEntrada1(contadorbin_1_led1), .LedEntrada2(contadorbin_1_led2), .LedEntrada3(contadorbin_1_led3),
    .LedEntrada4(contadorbin_1_led4), .LedEntrada5(contadorbin_1_led5), .LedEntrada6(contadorbin_1_led6),
    .LedEntrada7(contadorbin_1_led7), .LedEntrada8(contadorbin_1_led8), .LedEntrada9(contadorbin_1_led9),
    .LedEntrada10(contadorbin_1_led10), .ResetRecord(button_7_out), .Clock(Reloj),
    .Led1(puntajerecord_1_led1), .Led2(puntajerecord_1_led2), .Led3(puntajerecord_1_led3),
    .Led4(puntajerecord_1_led4), .Led5(puntajerecord_1_led5), .Led6(puntajerecord_1_led6),
    .Led7(puntajerecord_1_led7), .Led8(puntajerecord_1_led8), .Led9(puntajerecord_1_led9),
    .Led10(puntajerecord_1_led10));
  LED led_12 (.in(puntajerecord_1_led2));
  LED led_13 (.in(puntajerecord_1_led3));
  LED led_14 (.in(puntajerecord_1_led4));
  LED led_15 (.in(puntajerecord_1_led5));
  LED led_16 (.in(puntajerecord_1_led6));
  LED led_17 (.in(puntajerecord_1_led7));
  LED led_18 (.in(puntajerecord_1_led8));
  LED led_19 (.in(puntajerecord_1_led9));
  LED led_20 (.in(puntajerecord_1_led10));
  Hex_Digit_Display hex_digit_display_5 (.value(puntajerecordhexa_1_record4));  // open: dp
  PuntajeRecordHexa puntajerecordhexa_1 (
    .Puntos4(contador2_1_puntos4), .Puntos3(contador2_1_puntos3), .Puntos2(contador2_1_puntos2),
    .Puntos1(contador2_1_puntos1), .Reset(button_7_out), .Clock(Reloj),
    .Record4(puntajerecordhexa_1_record4), .Record3(puntajerecordhexa_1_record3),
    .Record2(puntajerecordhexa_1_record2), .Record1(puntajerecordhexa_1_record1));
  Hex_Digit_Display hex_digit_display_6 (.value(puntajerecordhexa_1_record3));  // open: dp
  Hex_Digit_Display hex_digit_display_7 (.value(puntajerecordhexa_1_record2));  // open: dp
  Hex_Digit_Display hex_digit_display_8 (.value(puntajerecordhexa_1_record1));  // open: dp

  // Notes on the sheet:
  //   Configurar el reloj en 8hz para iniciar el juego
  //   - velocidad 1: menos de 10 bloques
  //   - velocidad 2: entre 10 y 20 bloques
  //   - velocidad 3: mas de 20 bloques
  //   Puntaje Actual
  //   Puntaje Record
endmodule

module contadorBin (
  input  Entrada,
  input  Suma5,
  input  Reset,
  input  Clock,
  output Led1,
  output Led2,
  output Led3,
  output Led4,
  output Led5,
  output Led6,
  output Led7,
  output Led8,
  output Led9,
  output Led10
);

  wire and_1_out, and_2_out, and_3_out, and_4_out, and_5_out, and_6_out, and_7_out, and_8_out, and_9_out,
       decoder_1_out1, decoder_1_out3, decoder_1_out5, decoder_1_out7, decoder_1_out9, decoder_1_out10,
       not_1_out, or_1_out, or_2_out, or_3_out;
  wire [3:0] counter_1_q;

  Counter #(.max('ha), .width(4)) counter_1 (
    .D(4'b1010), .Q(counter_1_q), .up(Entrada), .clk(or_1_out));  // open: load, count, carry, clr
  or or_1 (or_1_out, Suma5, and_1_out);
  and and_1 (and_1_out, Clock, not_1_out);
  Decoder #(.select(4)) decoder_1 (
    .out1(decoder_1_out1), .out3(decoder_1_out3), .out5(decoder_1_out5), .out7(decoder_1_out7),
    .out9(decoder_1_out9), .out10(decoder_1_out10), .sel(counter_1_q));  // open: out0, out2, out4, out6, out8, out11, out12, out13, out14, out15, en
  not not_1 (not_1_out, decoder_1_out10);
  or or_2 (or_2_out, decoder_1_out1, decoder_1_out3, decoder_1_out5, decoder_1_out7, decoder_1_out9);
  or or_3 (or_3_out, or_2_out, Entrada);
  J_K_Flip_Flop j_k_ff_1 (.J(or_3_out), .K(or_3_out), .clk(or_3_out), .Q(Led1), .reset(Reset));  // open: Qn, preset
  and and_2 (and_2_out, Led1, Led2);
  J_K_Flip_Flop j_k_ff_2 (.J(Led1), .K(Led1), .clk(or_3_out), .Q(Led2), .reset(Reset));  // open: Qn, preset
  and and_3 (and_3_out, and_2_out, Led3);
  J_K_Flip_Flop j_k_ff_3 (.J(and_2_out), .K(and_2_out), .clk(or_3_out), .Q(Led3), .reset(Reset));  // open: Qn, preset
  J_K_Flip_Flop j_k_ff_4 (.J(and_3_out), .K(and_3_out), .clk(or_3_out), .Q(Led4), .reset(Reset));  // open: Qn, preset
  and and_4 (and_4_out, and_3_out, Led4);
  J_K_Flip_Flop j_k_ff_5 (.J(and_4_out), .K(and_4_out), .clk(or_3_out), .Q(Led5), .reset(Reset));  // open: Qn, preset
  and and_5 (and_5_out, and_4_out, Led5);
  and and_6 (and_6_out, and_5_out, Led6);
  J_K_Flip_Flop j_k_ff_6 (.J(and_5_out), .K(and_5_out), .clk(or_3_out), .Q(Led6), .reset(Reset));  // open: Qn, preset
  J_K_Flip_Flop j_k_ff_7 (.J(and_6_out), .K(and_6_out), .clk(or_3_out), .Q(Led7), .reset(Reset));  // open: Qn, preset
  and and_7 (and_7_out, and_6_out, Led7);
  and and_8 (and_8_out, and_7_out, Led8);
  J_K_Flip_Flop j_k_ff_8 (.J(and_7_out), .K(and_7_out), .clk(or_3_out), .Q(Led8), .reset(Reset));  // open: Qn, preset
  J_K_Flip_Flop j_k_ff_9 (.J(and_8_out), .K(and_8_out), .clk(or_3_out), .Q(Led9), .reset(Reset));  // open: Qn, preset
  and and_9 (and_9_out, and_8_out, Led9);
  J_K_Flip_Flop j_k_ff_10 (.J(and_9_out), .K(and_9_out), .clk(or_3_out), .Q(Led10), .reset(Reset));  // open: Qn, preset
endmodule

module contador2 (
  input  Reset,
  input  Suma5,
  input  Sumar1,
  input  Clock,
  output [3:0] Puntos4,
  output [3:0] Puntos3,
  output [3:0] Puntos2,
  output [3:0] Puntos1
);

  wire and_1_out, counter_3_carry, counter_4_carry, counter_5_carry, decoder_1_out1, decoder_1_out3,
       decoder_1_out5, decoder_1_out7, decoder_1_out9, decoder_1_out10, not_1_out, not_2_out, not_3_out,
       not_4_out, or_1_out, or_2_out, or_3_out;
  wire [3:0] counter_1_q;

  Counter #(.max('ha), .width(4)) counter_1 (
    .D(4'b1010), .Q(counter_1_q), .up(Sumar1), .clk(or_1_out));  // open: load, count, carry, clr
  or or_1 (or_1_out, Suma5, and_1_out);
  and and_1 (and_1_out, Clock, not_1_out);
  Decoder #(.select(4)) decoder_1 (
    .out1(decoder_1_out1), .out3(decoder_1_out3), .out5(decoder_1_out5), .out7(decoder_1_out7),
    .out9(decoder_1_out9), .out10(decoder_1_out10), .sel(counter_1_q));  // open: out0, out2, out4, out6, out8, out11, out12, out13, out14, out15, en
  not not_1 (not_1_out, decoder_1_out10);
  or or_2 (or_2_out, decoder_1_out1, decoder_1_out3, decoder_1_out5, decoder_1_out7, decoder_1_out9);
  Counter #(.max('h9), .width(4)) counter_2 (
    .clr(Reset), .clk(not_2_out), .Q(Puntos4));  // open: load, up, count, D, carry
  Counter #(.max('h9), .width(4)) counter_3 (
    .clr(Reset), .clk(not_3_out), .carry(counter_3_carry), .Q(Puntos3));  // open: load, up, count, D
  Counter #(.max('h9), .width(4)) counter_4 (
    .clr(Reset), .clk(not_4_out), .carry(counter_4_carry), .Q(Puntos2));  // open: load, up, count, D
  Counter #(.max('h9), .width(4)) counter_5 (
    .clr(Reset), .clk(or_3_out), .carry(counter_5_carry), .Q(Puntos1));  // open: load, up, count, D
  or or_3 (or_3_out, or_2_out, Sumar1);
  not not_2 (not_2_out, counter_3_carry);
  not not_3 (not_3_out, counter_4_carry);
  not not_4 (not_4_out, counter_5_carry);
endmodule

module PuntajeRecord (
  input  LedEntrada1,
  input  LedEntrada2,
  input  LedEntrada3,
  input  LedEntrada4,
  input  LedEntrada5,
  input  LedEntrada6,
  input  LedEntrada7,
  input  LedEntrada8,
  input  LedEntrada9,
  input  LedEntrada10,
  input  ResetRecord,
  input  Clock,
  output Led1,
  output Led2,
  output Led3,
  output Led4,
  output Led5,
  output Led6,
  output Led7,
  output Led8,
  output Led9,
  output Led10
);

  wire and_1_out, comparator_1_gt;
  wire [9:0] d_ff_18_q;

  D_Flip_Flop d_ff_1 (.D(LedEntrada10), .clk(Clock), .Q(d_ff_18_q[9]));  // open: Qn, preset, reset
  D_Flip_Flop d_ff_2 (.D(LedEntrada9), .clk(Clock), .Q(d_ff_18_q[8]));  // open: Qn, preset, reset
  D_Flip_Flop d_ff_3 (.D(d_ff_18_q[9]), .clk(and_1_out), .Q(Led10), .reset(ResetRecord));  // open: Qn, preset
  D_Flip_Flop d_ff_4 (.D(LedEntrada8), .clk(Clock), .Q(d_ff_18_q[7]));  // open: Qn, preset, reset
  D_Flip_Flop d_ff_5 (.D(d_ff_18_q[8]), .clk(and_1_out), .Q(Led9), .reset(ResetRecord));  // open: Qn, preset
  D_Flip_Flop d_ff_6 (.D(LedEntrada7), .clk(Clock), .Q(d_ff_18_q[6]));  // open: Qn, preset, reset
  D_Flip_Flop d_ff_7 (.D(d_ff_18_q[7]), .clk(and_1_out), .Q(Led8), .reset(ResetRecord));  // open: Qn, preset
  D_Flip_Flop d_ff_8 (.D(LedEntrada6), .clk(Clock), .Q(d_ff_18_q[5]));  // open: Qn, preset, reset
  D_Flip_Flop d_ff_9 (.D(d_ff_18_q[6]), .clk(and_1_out), .Q(Led7), .reset(ResetRecord));  // open: Qn, preset
  D_Flip_Flop d_ff_10 (.D(LedEntrada5), .clk(Clock), .Q(d_ff_18_q[4]));  // open: Qn, preset, reset
  D_Flip_Flop d_ff_11 (.D(d_ff_18_q[5]), .clk(and_1_out), .Q(Led6), .reset(ResetRecord));  // open: Qn, preset
  D_Flip_Flop d_ff_12 (.D(LedEntrada4), .clk(Clock), .Q(d_ff_18_q[3]));  // open: Qn, preset, reset
  D_Flip_Flop d_ff_13 (.D(d_ff_18_q[4]), .clk(and_1_out), .Q(Led5), .reset(ResetRecord));  // open: Qn, preset
  D_Flip_Flop d_ff_14 (.D(LedEntrada3), .clk(Clock), .Q(d_ff_18_q[2]));  // open: Qn, preset, reset
  D_Flip_Flop d_ff_15 (.D(d_ff_18_q[3]), .clk(and_1_out), .Q(Led4), .reset(ResetRecord));  // open: Qn, preset
  Comparator #(.mode("unsigned"), .width(10)) comparator_1 (
    .a(d_ff_18_q), .b({Led10, Led9, Led8, Led7, Led6, Led5, Led4, Led3, Led2, Led1}), .gt(comparator_1_gt));  // open: eq, lt
  D_Flip_Flop d_ff_16 (.D(d_ff_18_q[2]), .clk(and_1_out), .Q(Led3), .reset(ResetRecord));  // open: Qn, preset
  D_Flip_Flop d_ff_17 (.D(LedEntrada2), .clk(Clock), .Q(d_ff_18_q[1]));  // open: Qn, preset, reset
  D_Flip_Flop d_ff_18 (.D(LedEntrada1), .clk(Clock), .Q(d_ff_18_q[0]));  // open: Qn, preset, reset
  D_Flip_Flop d_ff_19 (.D(d_ff_18_q[1]), .clk(and_1_out), .Q(Led2), .reset(ResetRecord));  // open: Qn, preset
  D_Flip_Flop d_ff_20 (.D(d_ff_18_q[0]), .clk(and_1_out), .Q(Led1), .reset(ResetRecord));  // open: Qn, preset
  and and_1 (and_1_out, comparator_1_gt, Clock);
endmodule

module PuntajeRecordHexa (
  input  [3:0] Puntos4,
  input  [3:0] Puntos3,
  input  [3:0] Puntos2,
  input  [3:0] Puntos1,
  input  Reset,
  input  Clock,
  output [3:0] Record4,
  output [3:0] Record3,
  output [3:0] Record2,
  output [3:0] Record1
);

  wire and_1_out, and_2_out, and_3_out, comparator_1_eq, comparator_1_gt, comparator_2_eq, comparator_2_gt,
       comparator_3_eq, comparator_3_gt, comparator_4_gt, or_1_out;

  Register #(.width(4)) register_1 (.D(Puntos4), .en(or_1_out), .clk(Clock), .Q(Record4), .clr(Reset));
  Register #(.width(4)) register_2 (.D(Puntos3), .en(or_1_out), .clk(Clock), .Q(Record3));  // open: clr
  Register #(.width(4)) register_3 (.D(Puntos2), .en(or_1_out), .clk(Clock), .Q(Record2), .clr(Reset));
  Register #(.width(4)) register_4 (.D(Puntos1), .en(or_1_out), .clk(Clock), .Q(Record1), .clr(Reset));
  Comparator #(.mode("unsigned"), .width(4)) comparator_1 (
    .a(Puntos4), .b(Record4), .gt(comparator_1_gt), .eq(comparator_1_eq));  // open: lt
  Comparator #(.mode("unsigned"), .width(4)) comparator_2 (
    .a(Puntos3), .b(Record3), .gt(comparator_2_gt), .eq(comparator_2_eq));  // open: lt
  Comparator #(.mode("unsigned"), .width(4)) comparator_3 (
    .a(Puntos2), .b(Record2), .gt(comparator_3_gt), .eq(comparator_3_eq));  // open: lt
  Comparator #(.mode("unsigned"), .width(4)) comparator_4 (
    .a(Puntos1), .b(Record1), .gt(comparator_4_gt));  // open: eq, lt
  and and_1 (and_1_out, comparator_1_eq, comparator_2_gt);
  and and_2 (and_2_out, comparator_1_eq, comparator_2_eq, comparator_3_gt);
  and and_3 (and_3_out, comparator_1_eq, comparator_2_eq, comparator_3_eq, comparator_4_gt);
  or or_1 (or_1_out, comparator_1_gt, and_1_out, and_2_out, and_3_out);
endmodule

module movimientoCuadrado (
  input  colisionY,
  input  strart,
  input  Clock,
  input  izq,
  input  der,
  input  colisionIzq,
  input  colisionDer,
  output [4:0] inicio,
  output [7:0] col0,
  output [7:0] col1,
  output [7:0] col2,
  output [7:0] col3,
  output [7:0] col4,
  output [7:0] filaActual,
  output [2:0] colActual
);

  wire and_3_out, and_5_out, and_6_out, and_7_out, and_8_out, and_9_out, button_1_out, comparator_1_eq,
       comparator_2_gt, d_ff_1_q, d_ff_2_q, decoder_2_out0, decoder_2_out1, decoder_2_out2, decoder_2_out3,
       decoder_2_out4, not_1_out, not_2_out, not_3_out, not_4_out, not_5_out, not_6_out, not_7_out,
       not_8_out, not_9_out, not_10_out, or_1_out, or_2_out, or_3_out, or_4_out, or_5_out, random_1_p1,
       shift_register_2_out, shift_register_3_out, shift_register_4_out, shift_register_5_out,
       shift_register_6_out;
  wire [2:0] undriven;
  wire [7:0] shift_register_1_q7;

  Decoder #(.select(3)) decoder_1 (
    .out0(inicio[0]), .out1(inicio[3]), .out2(inicio[2]), .out3(inicio[1]), .out4(inicio[4]), .sel(undriven));  // open: out5, out6, out7, en
  DotMatrix #(.matrixrows(1)) dotmatrix_1 (
    .col0(inicio[0]), .col1(inicio[3]), .col2(inicio[2]), .col3(inicio[1]), .col4(inicio[4]));
  DotMatrix #(.matrixrows(8)) dotmatrix_2 (.col0(col0), .col1(col1), .col2(col2), .col3(col3), .col4(col4));
  Button button_1 (.out(button_1_out));
  or or_1 (or_1_out, strart, button_1_out);
  D_Flip_Flop d_ff_1 (.D(or_1_out), .clk(Clock), .Q(d_ff_1_q));  // open: Qn, preset, reset
  or or_2 (or_2_out, not_1_out, comparator_1_eq);
  not not_1 (not_1_out, comparator_2_gt);
  // AND_Gate and_1 has open pins: in0=not_2_out, out=open
  not not_2 (not_2_out, colisionIzq);
  // Random #(.width(3)) random_1: pin names not known; wires that end beside it: random_1_p1
  and and_2 (random_1_p1, or_2_out, not_5_out);
  and and_3 (and_3_out, comparator_2_gt, d_ff_2_q);
  Counter #(.max('h4), .ongoal("stay"), .width(3)) counter_1 (
    .load(and_3_out), .D(undriven), .count(or_3_out), .Q(colActual), .up(der), .clk(or_3_out));  // open: carry, clr
  or or_3 (or_3_out, izq, and_3_out, der);
  Comparator #(.mode("unsigned")) comparator_1 (
    .a(shift_register_1_q7), .b(8'h40), .eq(comparator_1_eq));  // open: gt, lt
  Comparator #(.mode("unsigned"), .width(3)) comparator_2 (
    .a(3'b101), .b(undriven), .gt(comparator_2_gt));  // open: eq, lt
  Decoder #(.select(3)) decoder_2 (
    .out0(decoder_2_out0), .out1(decoder_2_out1), .out2(decoder_2_out2), .out3(decoder_2_out3),
    .out4(decoder_2_out4), .sel(colActual));  // open: out5, out6, out7, en
  // AND_Gate and_4 has open pins: in1=not_3_out, out=open
  not not_3 (not_3_out, colisionDer);
  not not_4 (not_4_out, d_ff_2_q);
  not not_5 (not_5_out, Clock);
  or or_4 (or_4_out, d_ff_2_q, colisionY, d_ff_1_q);
  Shift_Register shift_register_1 (
    .shift(not_4_out), .in(1'b0), .clk(Clock), .load(or_4_out), .d0(1'b1), .q0(shift_register_1_q7[7]),
    .d1(1'b0), .q1(shift_register_1_q7[6]), .d2(1'b0), .q2(shift_register_1_q7[5]), .d3(1'b0),
    .q3(shift_register_1_q7[4]), .d4(1'b0), .q4(shift_register_1_q7[3]), .d5(1'b0),
    .q5(shift_register_1_q7[2]), .d6(1'b0), .q6(shift_register_1_q7[1]), .d7(1'b0),
    .q7(shift_register_1_q7[0]));  // open: out, clr
  and and_5 (and_5_out, not_5_out, decoder_2_out0);
  and and_6 (and_6_out, not_5_out, decoder_2_out1);
  and and_7 (and_7_out, not_5_out, decoder_2_out2);
  and and_8 (and_8_out, not_5_out, decoder_2_out3);
  and and_9 (and_9_out, not_5_out, decoder_2_out4);
  not not_6 (not_6_out, decoder_2_out0);
  not not_7 (not_7_out, decoder_2_out1);
  not not_8 (not_8_out, decoder_2_out2);
  not not_9 (not_9_out, decoder_2_out3);
  not not_10 (not_10_out, decoder_2_out4);
  Shift_Register shift_register_2 (
    .clk(and_5_out), .out(shift_register_2_out), .load(and_5_out), .clr(not_6_out),
    .d0(shift_register_1_q7[7]), .q0(col0[7]), .d1(shift_register_1_q7[6]), .q1(col0[6]),
    .d2(shift_register_1_q7[5]), .q2(col0[5]), .d3(shift_register_1_q7[4]), .q3(col0[4]),
    .d4(shift_register_1_q7[3]), .q4(col0[3]), .d5(shift_register_1_q7[2]), .q5(col0[2]),
    .d6(shift_register_1_q7[1]), .q6(col0[1]), .d7(shift_register_1_q7[0]), .q7(col0[0]));  // open: shift, in
  Shift_Register shift_register_3 (
    .clk(and_6_out), .out(shift_register_3_out), .load(and_6_out), .clr(not_7_out),
    .d0(shift_register_1_q7[7]), .q0(col1[7]), .d1(shift_register_1_q7[6]), .q1(col1[6]),
    .d2(shift_register_1_q7[5]), .q2(col1[5]), .d3(shift_register_1_q7[4]), .q3(col1[4]),
    .d4(shift_register_1_q7[3]), .q4(col1[3]), .d5(shift_register_1_q7[2]), .q5(col1[2]),
    .d6(shift_register_1_q7[1]), .q6(col1[1]), .d7(shift_register_1_q7[0]), .q7(col1[0]));  // open: shift, in
  Shift_Register shift_register_4 (
    .clk(and_7_out), .out(shift_register_4_out), .load(and_7_out), .clr(not_8_out),
    .d0(shift_register_1_q7[7]), .q0(col2[7]), .d1(shift_register_1_q7[6]), .q1(col2[6]),
    .d2(shift_register_1_q7[5]), .q2(col2[5]), .d3(shift_register_1_q7[4]), .q3(col2[4]),
    .d4(shift_register_1_q7[3]), .q4(col2[3]), .d5(shift_register_1_q7[2]), .q5(col2[2]),
    .d6(shift_register_1_q7[1]), .q6(col2[1]), .d7(shift_register_1_q7[0]), .q7(col2[0]));  // open: shift, in
  Shift_Register shift_register_5 (
    .clk(and_8_out), .out(shift_register_5_out), .load(and_8_out), .clr(not_9_out),
    .d0(shift_register_1_q7[7]), .q0(col3[7]), .d1(shift_register_1_q7[6]), .q1(col3[6]),
    .d2(shift_register_1_q7[5]), .q2(col3[5]), .d3(shift_register_1_q7[4]), .q3(col3[4]),
    .d4(shift_register_1_q7[3]), .q4(col3[3]), .d5(shift_register_1_q7[2]), .q5(col3[2]),
    .d6(shift_register_1_q7[1]), .q6(col3[1]), .d7(shift_register_1_q7[0]), .q7(col3[0]));  // open: shift, in
  Shift_Register shift_register_6 (
    .clk(and_9_out), .out(shift_register_6_out), .load(and_9_out), .clr(not_10_out),
    .d0(shift_register_1_q7[7]), .q0(col4[7]), .d1(shift_register_1_q7[6]), .q1(col4[6]),
    .d2(shift_register_1_q7[5]), .q2(col4[5]), .d3(shift_register_1_q7[4]), .q3(col4[4]),
    .d4(shift_register_1_q7[3]), .q4(col4[3]), .d5(shift_register_1_q7[2]), .q5(col4[2]),
    .d6(shift_register_1_q7[1]), .q6(col4[1]), .d7(shift_register_1_q7[0]), .q7(col4[0]));  // open: shift, in
  or or_5 (or_5_out, shift_register_2_out, shift_register_3_out, shift_register_4_out, shift_register_5_out, shift_register_6_out);
  D_Flip_Flop d_ff_2 (.D(or_5_out), .clk(not_5_out), .Q(d_ff_2_q));  // open: Qn, preset, reset
  Multiplexer #(.select(3), .width(8)) multiplexer_1 (
    .in0(col0), .in1(col1), .in2(col2), .in3(col3), .in4(col4), .out(filaActual), .sel(colActual));  // open: in5, in6, in7
endmodule

module guardarNuevoEstado (
  input  CLK,
  input  RESET,
  input  WRITE_ENABLE,
  input  [7:0] Y_POS,
  input  [2:0] X_POS,
  output [7:0] COL_0,
  output [7:0] COL_1,
  output [7:0] COL_2,
  output [7:0] COL_3,
  output [7:0] COL_4,
  output NEXT_BIT_TRIGGER,
  output colisionY,
  output colisionDer,
  output colisionIzq
);

  wire and_2_out, and_3_out, and_4_out, and_5_out, and_6_out, and_7_out, and_8_out, and_9_out, and_10_out,
       and_11_out, and_12_out, and_13_out, and_14_out, comparator_1_eq, comparator_1_lt, comparator_2_eq,
       comparator_2_lt, comparator_3_eq, comparator_3_lt, comparator_4_eq, comparator_4_lt, comparator_5_eq,
       comparator_5_lt, decoder_1_out0, decoder_1_out1, decoder_1_out2, decoder_1_out3, decoder_1_out4,
       or_1_out, or_2_out, or_3_out, or_4_out, or_5_out, t_ff_1_q;
  wire [2:0] REG_X_q;
  wire [4:0] decoder_2_out0;
  wire [7:0] adder_1_out, multiplexer_1_out, or_7_out, or_9_out, or_10_out, or_11_out, or_12_out, REG_Y_q;

  T_Flip_Flop t_ff_1 (.T(WRITE_ENABLE), .clk(WRITE_ENABLE), .Q(t_ff_1_q));  // open: Qn, reset, preset
  and and_1 (NEXT_BIT_TRIGGER, t_ff_1_q, colisionY);
  Register REG_Y (.D(Y_POS), .en(NEXT_BIT_TRIGGER), .clk(CLK), .Q(REG_Y_q), .clr(RESET));
  Register #(.width(3)) REG_X (.D(X_POS), .en(NEXT_BIT_TRIGGER), .clk(CLK), .Q(REG_X_q), .clr(RESET));
  Comparator #(.mode("unsigned")) comparator_1 (
    .a(Y_POS), .b(COL_0), .eq(comparator_1_eq), .lt(comparator_1_lt));  // open: gt
  Comparator #(.mode("unsigned")) comparator_2 (
    .a(Y_POS), .b(COL_1), .eq(comparator_2_eq), .lt(comparator_2_lt));  // open: gt
  Comparator #(.mode("unsigned")) comparator_3 (
    .a(Y_POS), .b(COL_2), .eq(comparator_3_eq), .lt(comparator_3_lt));  // open: gt
  Comparator #(.mode("unsigned")) comparator_4 (
    .a(Y_POS), .b(COL_3), .eq(comparator_4_eq), .lt(comparator_4_lt));  // open: gt
  Comparator #(.mode("unsigned")) comparator_5 (
    .a(Y_POS), .b(COL_4), .eq(comparator_5_eq), .lt(comparator_5_lt));  // open: gt
  Comparator #(.mode("unsigned")) comparator_6 (.a(Y_POS), .b(8'h3));  // open: gt, eq, lt
  Decoder #(.select(3)) decoder_1 (
    .out0(decoder_1_out0), .out1(decoder_1_out1), .out2(decoder_1_out2), .out3(decoder_1_out3),
    .out4(decoder_1_out4), .sel(X_POS));  // open: out5, out6, out7, en
  Decoder #(.select(3)) decoder_2 (
    .out0(decoder_2_out0[0]), .out1(decoder_2_out0[1]), .out2(decoder_2_out0[2]), .out3(decoder_2_out0[3]),
    .out4(decoder_2_out0[4]), .sel(REG_X_q), .en(1'b1));  // open: out5, out6, out7
  or or_1 (or_1_out, comparator_1_eq, comparator_1_lt);
  or or_2 (or_2_out, comparator_2_eq, comparator_2_lt);
  or or_3 (or_3_out, comparator_3_eq, comparator_3_lt);
  or or_4 (or_4_out, comparator_4_eq, comparator_4_lt);
  or or_5 (or_5_out, comparator_5_eq, comparator_5_lt);
  and and_2 (and_2_out, decoder_1_out0, or_2_out);
  and and_3 (and_3_out, decoder_1_out1, or_3_out);
  and and_4 (and_4_out, decoder_1_out2, or_4_out);
  and and_5 (and_5_out, decoder_1_out3, or_5_out);
  or or_6 (colisionDer, and_2_out, and_3_out, and_4_out, and_5_out);
  assign or_7_out = COL_0 | REG_Y_q;  // OR_Gate or_7, 8 bits wide
  and and_6 (and_6_out, NEXT_BIT_TRIGGER, decoder_2_out0[0]);
  and and_7 (and_7_out, or_1_out, decoder_1_out1);
  and and_8 (and_8_out, or_2_out, decoder_1_out2);
  and and_9 (and_9_out, or_3_out, decoder_1_out3);
  and and_10 (and_10_out, or_4_out, decoder_1_out4);
  Register register_1 (.D(or_7_out), .en(and_6_out), .Q(COL_0), .clk(CLK), .clr(RESET));
  or or_8 (colisionIzq, and_7_out, and_8_out, and_9_out, and_10_out);
  assign or_9_out = COL_1 | REG_Y_q;  // OR_Gate or_9, 8 bits wide
  and and_11 (and_11_out, NEXT_BIT_TRIGGER, decoder_2_out0[1]);
  Register register_2 (.D(or_9_out), .en(and_11_out), .Q(COL_1), .clk(CLK), .clr(RESET));
  assign or_10_out = COL_2 | REG_Y_q;  // OR_Gate or_10, 8 bits wide
  and and_12 (and_12_out, NEXT_BIT_TRIGGER, decoder_2_out0[2]);
  Multiplexer #(.select(3), .width(8)) multiplexer_1 (
    .in0(COL_0), .in1(COL_1), .in2(COL_2), .in3(COL_3), .in4(COL_4), .out(multiplexer_1_out), .sel(X_POS));  // open: in5, in6, in7
  Register register_3 (.D(or_10_out), .en(and_12_out), .Q(COL_2), .clk(CLK), .clr(RESET));
  Adder adder_1 (.a(multiplexer_1_out), .b(8'h1), .out(adder_1_out));  // open: cin, cout
  assign or_11_out = COL_3 | REG_Y_q;  // OR_Gate or_11, 8 bits wide
  and and_13 (and_13_out, NEXT_BIT_TRIGGER, decoder_2_out0[3]);
  Comparator comparator_7 (.a(adder_1_out), .b(Y_POS), .eq(colisionY));  // open: gt, lt
  Register register_4 (.D(or_11_out), .en(and_13_out), .Q(COL_3), .clk(CLK), .clr(RESET));
  assign or_12_out = COL_4 | REG_Y_q;  // OR_Gate or_12, 8 bits wide
  and and_14 (and_14_out, NEXT_BIT_TRIGGER, decoder_2_out0[4]);
  Register register_5 (.D(or_12_out), .en(and_14_out), .Q(COL_4), .clk(CLK), .clr(RESET));
endmodule

module colisionesMemoria (
  input  [2:0] colActual,
  input  [7:0] filaActual
);

  wire clock_2_out, comparator_1_eq, comparator_2_eq;
  wire [7:0] ram_1_dout;

  Clock clock_1 ();  // open: out
  Comparator comparator_1 (.a(filaActual), .b(8'h1), .eq(comparator_1_eq));  // open: gt, lt
  Clock clock_2 (.out(clock_2_out));
  RAM #(.addrWidth(3)) ram_1 (
    .addr(colActual), .clk(clock_2_out), .din(filaActual), .dout(ram_1_dout));  // open: we, oe
  Comparator comparator_2 (.a(ram_1_dout), .b({8{1'b0}}), .eq(comparator_2_eq));  // open: gt, lt
endmodule

module ReductorFrecuencia2 (
  input  Reloj,
  input  Activador,
  input  Reset,
  output RelojDividido
);

  wire and_1_out, not_1_out;

  and and_1 (and_1_out, Reloj, Activador);
  Register #(.width(1)) register_1 (.D(not_1_out), .en(1'b1), .clk(and_1_out), .Q(RelojDividido), .clr(Reset));
  not not_1 (not_1_out, RelojDividido);
endmodule

module ReductorFrecuencia4 (
  input  Reloj,
  input  Activador,
  input  Reset,
  output RelojDividido
);

  wire and_1_out, not_1_out, not_2_out, register_1_q;

  and and_1 (and_1_out, Reloj, Activador);
  Register #(.width(1)) register_1 (.D(not_1_out), .en(1'b1), .clk(and_1_out), .Q(register_1_q), .clr(Reset));
  not not_1 (not_1_out, register_1_q);
  Register #(.width(1)) register_2 (.D(not_2_out), .en(1'b1), .clk(register_1_q), .Q(RelojDividido), .clr(Reset));
  not not_2 (not_2_out, RelojDividido);
endmodule

module ReductorFrecuencia8 (
  input  Reloj,
  input  Activador,
  input  Reset,
  output RelojDividido
);

  wire and_1_out, not_1_out, not_2_out, not_3_out, register_1_q, register_2_q;

  and and_1 (and_1_out, Reloj, Activador);
  Register #(.width(1)) register_1 (.D(not_1_out), .en(1'b1), .clk(and_1_out), .Q(register_1_q), .clr(Reset));
  not not_1 (not_1_out, register_1_q);
  Register #(.width(1)) register_2 (.D(not_2_out), .en(1'b1), .clk(register_1_q), .Q(register_2_q), .clr(Reset));
  not not_2 (not_2_out, register_2_q);
  Register #(.width(1)) register_3 (.D(not_3_out), .en(1'b1), .clk(register_2_q), .Q(RelojDividido), .clr(Reset));
  not not_3 (not_3_out, RelojDividido);
endmodule

module NivelVelocidad (
  input  Entrada,
  input  Reset,
  output velocidad1,
  output velocidad2,
  output velocidad3
);

  wire comparator_1_eq, comparator_1_gt, comparator_1_lt, comparator_2_eq, comparator_2_gt, comparator_2_lt,
       or_1_out;
  wire [4:0] counter_1_q;

  Counter #(.max('h1e), .ongoal("stay"), .width(5)) counter_1 (
    .Q(counter_1_q), .clk(Entrada), .clr(Reset));  // open: load, D, count, carry, up
  Comparator #(.mode("unsigned"), .width(5)) comparator_1 (
    .a(counter_1_q), .b(5'b01010), .gt(comparator_1_gt), .eq(comparator_1_eq), .lt(comparator_1_lt));
  Comparator #(.mode("unsigned"), .width(5)) comparator_2 (
    .a(counter_1_q), .b(5'b10100), .gt(comparator_2_gt), .eq(comparator_2_eq), .lt(comparator_2_lt));
  or or_1 (or_1_out, comparator_1_gt, comparator_1_eq);
  or or_2 (velocidad3, comparator_2_gt, comparator_2_eq);
  and and_1 (velocidad1, comparator_1_lt, comparator_2_lt);
  and and_2 (velocidad2, or_1_out, comparator_2_lt);
endmodule

module DetectorFilaCompleta (
  input  [7:0] COL0,
  input  [7:0] COL1,
  input  [7:0] COL2,
  input  [7:0] COL3,
  input  [7:0] COL4
);

  wire and_1_out, and_2_out, clock_1_out, comparator_1_gt, comparator_2_gt, comparator_3_gt, comparator_4_gt,
       comparator_5_gt, d_ff_1_q, d_ff_1_qn, not_1_out;
  wire [7:0] shift_register_1_q0, shift_register_2_q0, shift_register_3_q0, shift_register_4_q0,
       shift_register_5_q0;

  Clock clock_1 (.out(clock_1_out));
  Comparator comparator_1 (.a(COL0), .b({8{1'b0}}), .gt(comparator_1_gt));  // open: eq, lt
  Comparator comparator_2 (.a(COL1), .b({8{1'b0}}), .gt(comparator_2_gt));  // open: eq, lt
  Comparator comparator_3 (.a(COL2), .b({8{1'b0}}), .gt(comparator_3_gt));  // open: eq, lt
  Comparator comparator_4 (.a(COL3), .b({8{1'b0}}), .gt(comparator_4_gt));  // open: eq, lt
  Comparator comparator_5 (.a(COL4), .b({8{1'b0}}), .gt(comparator_5_gt));  // open: eq, lt
  D_Flip_Flop d_ff_1 (.D(and_1_out), .clk(clock_1_out), .Q(d_ff_1_q), .Qn(d_ff_1_qn));  // open: preset, reset
  and and_1 (and_1_out, comparator_1_gt, comparator_2_gt, comparator_3_gt, comparator_4_gt, comparator_5_gt, d_ff_1_qn);
  and and_2 (and_2_out, d_ff_1_q, clock_1_out);
  not not_1 (not_1_out, d_ff_1_q);
  Shift_Register shift_register_1 (
    .shift(not_1_out), .clk(and_2_out), .load(d_ff_1_q), .d0(COL0[7]), .q0(shift_register_1_q0[0]),
    .d1(COL0[6]), .q1(shift_register_1_q0[1]), .d2(COL0[5]), .q2(shift_register_1_q0[2]), .d3(COL0[4]),
    .q3(shift_register_1_q0[3]), .d4(COL0[3]), .q4(shift_register_1_q0[4]), .d5(COL0[2]),
    .q5(shift_register_1_q0[5]), .d6(COL0[1]), .q6(shift_register_1_q0[6]), .d7(COL0[0]),
    .q7(shift_register_1_q0[7]));  // open: in, out, clr
  Shift_Register shift_register_2 (
    .shift(not_1_out), .clk(and_2_out), .load(d_ff_1_q), .d0(COL1[7]), .q0(shift_register_2_q0[0]),
    .d1(COL1[6]), .q1(shift_register_2_q0[1]), .d2(COL1[5]), .q2(shift_register_2_q0[2]), .d3(COL1[4]),
    .q3(shift_register_2_q0[3]), .d4(COL1[3]), .q4(shift_register_2_q0[4]), .d5(COL1[2]),
    .q5(shift_register_2_q0[5]), .d6(COL1[1]), .q6(shift_register_2_q0[6]), .d7(COL1[0]),
    .q7(shift_register_2_q0[7]));  // open: in, out, clr
  Shift_Register shift_register_3 (
    .shift(not_1_out), .clk(and_2_out), .load(d_ff_1_q), .d0(COL2[7]), .q0(shift_register_3_q0[0]),
    .d1(COL2[6]), .q1(shift_register_3_q0[1]), .d2(COL2[5]), .q2(shift_register_3_q0[2]), .d3(COL2[4]),
    .q3(shift_register_3_q0[3]), .d4(COL2[3]), .q4(shift_register_3_q0[4]), .d5(COL2[2]),
    .q5(shift_register_3_q0[5]), .d6(COL2[1]), .q6(shift_register_3_q0[6]), .d7(COL2[0]),
    .q7(shift_register_3_q0[7]));  // open: in, out, clr
  Shift_Register shift_register_4 (
    .shift(not_1_out), .clk(and_2_out), .load(d_ff_1_q), .d0(COL3[7]), .q0(shift_register_4_q0[0]),
    .d1(COL3[6]), .q1(shift_register_4_q0[1]), .d2(COL3[5]), .q2(shift_register_4_q0[2]), .d3(COL3[4]),
    .q3(shift_register_4_q0[3]), .d4(COL3[3]), .q4(shift_register_4_q0[4]), .d5(COL3[2]),
    .q5(shift_register_4_q0[5]), .d6(COL3[1]), .q6(shift_register_4_q0[6]), .d7(COL3[0]),
    .q7(shift_register_4_q0[7]));  // open: in, out, clr
  Shift_Register shift_register_5 (
    .shift(not_1_out), .clk(and_2_out), .load(d_ff_1_q), .d0(COL4[7]), .q0(shift_register_5_q0[0]),
    .d1(COL4[6]), .q1(shift_register_5_q0[1]), .d2(COL4[5]), .q2(shift_register_5_q0[2]), .d3(COL4[4]),
    .q3(shift_register_5_q0[3]), .d4(COL4[3]), .q4(shift_register_5_q0[4]), .d5(COL4[2]),
    .q5(shift_register_5_q0[5]), .d6(COL4[1]), .q6(shift_register_5_q0[6]), .d7(COL4[0]),
    .q7(shift_register_5_q0[7]));  // open: in, out, clr
endmodule

module ManejoVelocidades (
  input  clk,
  input  entrada,
  input  reset,
  output salida
);

  wire and_1_out, nivelvelocidad_1_velocidad1, nivelvelocidad_1_velocidad2, nivelvelocidad_1_velocidad3,
       or_1_out, or_2_out, reductorfrecuencia2_1_relojdividido, reductorfrecuencia4_1_relojdividido;

  NivelVelocidad nivelvelocidad_1 (
    .Entrada(entrada), .Reset(reset), .velocidad1(nivelvelocidad_1_velocidad1),
    .velocidad2(nivelvelocidad_1_velocidad2), .velocidad3(nivelvelocidad_1_velocidad3));
  or or_1 (or_1_out, nivelvelocidad_1_velocidad2, reset);
  or or_2 (or_2_out, nivelvelocidad_1_velocidad3, reset);
  and and_1 (and_1_out, clk, nivelvelocidad_1_velocidad3);
  ReductorFrecuencia4 reductorfrecuencia4_1 (
    .Reloj(clk), .Activador(nivelvelocidad_1_velocidad1), .Reset(or_1_out),
    .RelojDividido(reductorfrecuencia4_1_relojdividido));
  ReductorFrecuencia2 reductorfrecuencia2_1 (
    .Reloj(clk), .Activador(nivelvelocidad_1_velocidad2), .Reset(or_2_out),
    .RelojDividido(reductorfrecuencia2_1_relojdividido));
  or or_3 (salida, reductorfrecuencia4_1_relojdividido, reductorfrecuencia2_1_relojdividido, and_1_out);
endmodule

module mergeTableros (
  input  [7:0] MC_C0,
  input  [7:0] GNE_C0,
  input  [7:0] MC_C1,
  input  [7:0] GNE_C1,
  input  [7:0] MC_C2,
  input  [7:0] GNE_C2,
  input  [7:0] MC_C3,
  input  [7:0] GNE_C3,
  input  [7:0] MC_C4,
  input  [7:0] GNE_C4,
  output [7:0] C0,
  output [7:0] C1,
  output [7:0] C2,
  output [7:0] C3,
  output [7:0] C4
);

  assign C0 = MC_C0 ^ GNE_C0;  // XOR_Gate xor_1, 8 bits wide
  assign C1 = MC_C1 ^ GNE_C1;  // XOR_Gate xor_2, 8 bits wide
  assign C2 = MC_C2 ^ GNE_C2;  // XOR_Gate xor_3, 8 bits wide
  assign C3 = MC_C3 ^ GNE_C3;  // XOR_Gate xor_4, 8 bits wide
  assign C4 = MC_C4 ^ GNE_C4;  // XOR_Gate xor_5, 8 bits wide
endmodule
